# Fritzing sketch powerfulsecuritysirenpcb1 (saved by Fritzing 0.9.6b)
circuit board: 14.0242cm x 6.41727cm

parts:
  R1 = Resistor [tolerance=±5% power=0.25 resistance=220k package=THT]
  R2 = Resistor [tolerance=±5% power=0.25 resistance=1k package=THT]
  R3 = Resistor [tolerance=±5% power=0.25 resistance=10k package=THT]
  C1 = Electrolytic Capacitor [capacitance=22µF voltage=35V package="100 mil [THT, electrolytic]"]
  R4 = Resistor [tolerance=±5% power=0.25 resistance=1k package=THT]
  R5 = Resistor [tolerance=±5% power=0.25 resistance=10k package=THT]
  R6 = Resistor [tolerance=±5% power=0.25 resistance=220k package=THT]
  R7 = Resistor [tolerance=±5% power=0.25 resistance=22k package=THT]
  R8 = Resistor [tolerance=±5% power=0.25 resistance=100k package=THT]
  C2 = Electrolytic Capacitor [capacitance=22µF voltage=35V package="100 mil [THT, electrolytic]"]
  C3 = Ceramic Capacitor [capacitance=10nF voltage=35V package="100 mil [THT, multilayer]"]
  SP1 = SPEAKER [package=pcb_mount_speaker]
  C4 = Electrolytic Capacitor [capacitance=47µF voltage=0.1kV package="100 mil [THT, electrolytic]"]
  VCC1 = Battery block 9V
  U1 = SWITCH-SPST-2 [package=switch-spst-vertical]
  S2 = Round Pushbutton
  Q1 = PNP-Transistor [package="TO92 [THT]"]
  Q2 = PNP-Transistor [package="TO92 [THT]"]
  Q3 = NPN-Transistor [package="TO92 [THT]"]

nets:
  N1: R1.Pin_0, R5.Pin_1, Q3.B
  N2: R1.Pin_1, Q2.C
  N3: R2.Pin_0, R3.Pin_1, R4.Pin_0, R5.Pin_0, R8.Pin_0, C2.-, SP1.+, C4.-, C4.+, VCC1.-, U1.O, S2.leg0, Q1.E, Q2.E, Q3.E
  N4: R2.Pin_1, Q1.C
  N5: R3.Pin_0, C1.+, Q1.B
  N6: C1.-, R4.Pin_1
  N7: R6.Pin_0, C2.+
  N8: R6.Pin_1, R7.Pin_0, Q2.B
  N9: R7.Pin_1, C3.0, C3.1, SP1.-, Q3.C
  N10: R8.Pin_1, S2.leg1
  N11: VCC1.+, U1.P
