# Fritzing sketch rain alarm  (saved by Fritzing 0.9.6b)
circuit board: 14.9889cm x 7.6843cm

parts:
  R1 = Resistor [tolerance=±20% power=0.25 resistance=10k package=THT]
  R2 = Resistor [tolerance=±5% power=0.25 resistance=100k package=THT]
  R3 = Resistor [tolerance=±20% power=0.25 resistance=47k package=THT]
  R4 = Resistor [tolerance=±5% power=0.25 resistance=33k package=THT]
  R5 = Resistor [tolerance=±5% power=0.25 resistance=1k package=THT]
  U2 = 555 Timer [package="SO8 [SMD]"]
  Part1 = Soil Moisture Sensor
  Q1 = PNP-Transistor [package="TO92 [THT]"]
  Q2 = NPN-Transistor [package="TO92 [THT]"]
  Q3 = NPN-Transistor [package="TO92 [THT]"]
  C1 = Ceramic Capacitor [capacitance=10nF voltage=35V package="100 mil [THT, multilayer]"]
  C2 = Ceramic Capacitor [capacitance=10nF voltage=35V package="100 mil [THT, multilayer]"]
  SP1 = SPEAKER [package=pcb_mount_speaker]
  VCC1 = Battery block 9V
  R6 = Resistor [tolerance=±5% power=0.25 resistance=39 package=THT]

nets:
  N1: R1.Pin_0, Part1.VCC
  N2: R1.Pin_1, R2.Pin_1, Q1.E, VCC1.+, R6.Pin_1
  N3: R2.Pin_0, R3.Pin_1, Q1.B
  N4: R3.Pin_0, Part1.SIG, Q3.B, Q3.C
  N5: R4.Pin_0, U2.Pin_2, U2.Pin_6, U2.Pin_7, C1.1
  N6: R4.Pin_1, R5.Pin_1, U2.Pin_3, U2.Pin_4, U2.Pin_8, Q1.C
  N7: R5.Pin_0, Q2.B
  N8: U2.Pin_1, Part1.GND, Q2.E, Q3.E, C1.0, C2.0, VCC1.-
  N9: U2.Pin_5, C2.1
  N10: Q2.C, SP1.-
  N11: SP1.+, R6.Pin_0
